# Fritzing sketch PrimoModulo (saved by Fritzing 0.9.3b)
breadboards: 1

parts:
  Digispark1 = Digispark
  R1 = Rotary Potentiometer (Large) [maximum_resistance=100kΩ package=THT]
  J1 = Piezo Speaker
  R2 = Resistor [tolerance=±5% resistance=220 package=THT]

nets:
  N1: Digispark1.VCC, R1.leg1
  N2: Digispark1.GND, R1.leg2, J1.pin1
  N3: Digispark1.P1, R1.wiper
  N4: Digispark1.P5, R2.Pin_1
  N5: J1.pin2, R2.Pin_0

custom parts:
  Digispark: The Digispark is an Attiny85 based microcontroller development board similar to the Arduino line, only cheaper, smaller, and a bit less powerful. With a whole host of shields to extend its functionality and the ability to use the familiar Arduino IDE the Digispark is a great way to jump into electronics, or perfect for when an Arduino is too big or too much.
