# Fritzing sketch SecondoModulo (saved by Fritzing 0.9.3b)
breadboards: 1

parts:
  Digispark2 = Digispark
  S1 = Pushbutton [package="[THT]"]
  LED1 = LED - 5mm [color="Red (633nm)" package="5 mm [THT]"]
  R1 = Resistor [tolerance=±5% resistance=220 package=THT]

nets:
  N1: Digispark2.VCC, S1.Pin_3, S1.Pin_4
  N2: Digispark2.GND, LED1.cathode, R1.Pin_1
  N3: Digispark2.P0, LED1.anode
  N4: Digispark2.P1, S1.Pin_1, S1.Pin_2, R1.Pin_0

custom parts:
  Digispark: The Digispark is an Attiny85 based microcontroller development board similar to the Arduino line, only cheaper, smaller, and a bit less powerful. With a whole host of shields to extend its functionality and the ability to use the familiar Arduino IDE the Digispark is a great way to jump into electronics, or perfect for when an Arduino is too big or too much.
