# Fritzing sketch TerzoModulo (saved by Fritzing 0.9.3b)
breadboards: 1

parts:
  Digispark3 = Digispark
  U1 = POT [package=pot_mammoth]
  LED2 = RGB LED (com. cathode, rbg) [package="5 mm [THT]"]
  R1 = Resistor [tolerance=±5% resistance=220 package=THT]
  R2 = Resistor [tolerance=±5% resistance=220 package=THT]
  R3 = Resistor [tolerance=±5% resistance=220 package=THT]

nets:
  N1: Digispark3.VCC, U1.S, LED2.common_cathode
  N2: Digispark3.GND, U1.E
  N3: Digispark3.P0, R1.Pin_1
  N4: Digispark3.P1, R3.Pin_1
  N5: Digispark3.P2, U1.A
  N6: Digispark3.P3, R2.Pin_1
  N7: LED2.red_anode, R1.Pin_0
  N8: LED2.blue_anode, R3.Pin_0
  N9: LED2.green_anode, R2.Pin_0

custom parts:
  Digispark: The Digispark is an Attiny85 based microcontroller development board similar to the Arduino line, only cheaper, smaller, and a bit less powerful. With a whole host of shields to extend its functionality and the ability to use the familiar Arduino IDE the Digispark is a great way to jump into electronics, or perfect for when an Arduino is too big or too much.
